// Logisim project s-mips.circ as structural Verilog
module S_MIPS_Board (
  input  DESHABILITAR_DISPATCHER,
  output halt
);

  wire button_1_out, CLK, CS, d_ff_1_q, LCLR, LoadRAM, LoadRAMOn, LW, R_R_W, R_W, ram_dispatcher_1_finished,
       RCS, Reset_out, RST, TTY_EN;
  wire [2:0] KDB;
  wire [3:0] LMask, Mask, ram_1_read_time, ram_1_write_time, RMask;
  wire [6:0] KDB_DATA, TTY_DATA;
  wire [15:0] Addr, LAddr, RAddr;
  wire [31:0] I0, I1, I2, I3, LData, ram_1_data_out_0, ram_1_data_out_1, ram_1_data_out_2, ram_1_data_out_3,
       RI0, RI1, RI2, RI3;

  TTY #(.rows(25), .cols(80)) tty_1 (.data(TTY_DATA), .clk(CLK), .we(TTY_EN), .clr(RST));
  not not_1 (LoadRAMOn, ram_dispatcher_1_finished);
  RAM_Dispatcher ram_dispatcher_1 (
    .WriteTime(ram_1_write_time), .Clock(CLK), .Data(LData), .Address(LAddr), .Mask(LMask),
    .Finished(ram_dispatcher_1_finished), .Write(LW), .CLR(LCLR));
  Keyboard #(.buflen(64)) keyboard_1 (.clk(CLK), .re(KDB[0]), .avail(KDB[2]), .data(KDB_DATA));  // open: clr
  RAM ram_1 (
    .Address(RAddr), .Data_Out_0(ram_1_data_out_0), .Data_Out_1(ram_1_data_out_1),
    .Data_Out_2(ram_1_data_out_2), .Data_Out_3(ram_1_data_out_3), .Data_In_0(RI0), .Data_In_1(RI1),
    .Data_In_2(RI2), .Data_In_3(RI3), .Mask(RMask), .nRead_Write(R_R_W), .Chip_Select(RCS),
    .Read_Time(ram_1_read_time), .Reset(button_1_out), .Write_Time(ram_1_write_time));
  Button button_1 (.out(button_1_out));
  D_Flip_Flop d_ff_1 (.clk(CLK), .D(1'b1), .Q(d_ff_1_q), .reset(Reset_out));  // open: Qn, preset, en
  Button Reset (.out(Reset_out));
  S_MIPS s_mips_1 (
    .Kbd_Enable(KDB[0]), .Address(Addr), .Kbd_Clear(KDB[1]), .Kbd_Available(KDB[2]), .RAM_In_0(I0),
    .Kbd_ASCII_Data(KDB_DATA), .RAM_In_1(I1), .TTY_Enable(TTY_EN), .RAM_In_2(I2), .RAM_In_3(I3),
    .TTY_ASCII_Data(TTY_DATA), .Reset(RST), .RAM_Out_0(ram_1_data_out_0), .Clock(CLK),
    .RAM_Out_1(ram_1_data_out_1), .Stop(halt), .RAM_Out_2(ram_1_data_out_2), .RAM_Out_3(ram_1_data_out_3),
    .Mask(Mask), .Read_Time(ram_1_read_time), .Write_Time(ram_1_write_time), .nRead_Write(R_W),
    .Chip_Select(CS));
  D_Flip_Flop d_ff_2 (.clk(CLK), .D(d_ff_1_q), .Qn(LCLR), .reset(Reset_out));  // open: Q, preset, en
  or or_1 (RST, LCLR, LoadRAM);
  Clock clock_1 (.out(CLK));
  Multiplexer #(.width(32), .enable("false")) multiplexer_1 (.in0(I0), .in1(LData), .out(RI0), .sel(LoadRAM));
  Multiplexer #(.width(32), .enable("false")) multiplexer_2 (.in0(I1), .in1(LData), .out(RI1), .sel(LoadRAM));
  Multiplexer #(.width(32), .enable("false")) multiplexer_3 (.in0(I2), .in1(LData), .out(RI2), .sel(LoadRAM));
  Multiplexer #(.width(32), .enable("false")) multiplexer_4 (.in0(I3), .in1(LData), .out(RI3), .sel(LoadRAM));
  and and_1 (LoadRAM, ~DESHABILITAR_DISPATCHER, LoadRAMOn);  // AND_Gate
  Multiplexer #(.width(16), .enable("false")) multiplexer_5 (.in0(Addr), .in1(LAddr), .out(RAddr), .sel(LoadRAM));
  Multiplexer #(.width(4), .enable("false")) multiplexer_6 (.in0(Mask), .in1(LMask), .out(RMask), .sel(LoadRAM));
  Multiplexer #(.enable("false")) multiplexer_7 (.in0(CS), .in1(LW), .out(RCS), .sel(LoadRAM));
  Multiplexer #(.enable("false")) multiplexer_8 (.in0(R_W), .in1(LW), .out(R_R_W), .sel(LoadRAM));

  // Notes on the sheet:
  //   NO MODIFICAR
  //   Keyboard
endmodule

module RAM (
  input  [15:0] Address,
  input  [31:0] Data_In_0,
  input  [31:0] Data_In_1,
  input  [31:0] Data_In_2,
  input  [31:0] Data_In_3,
  input  [3:0] Mask,
  input  nRead_Write,
  input  Chip_Select,
  input  Reset,
  output [31:0] Data_Out_0,
  output [31:0] Data_Out_1,
  output [31:0] Data_Out_2,
  output [31:0] Data_Out_3,
  output [3:0] Read_Time,
  output [3:0] Write_Time
);

  wire and_2_out, and_3_out, and_4_out, and_5_out, and_6_out, and_7_out, and_8_out, and_9_out, Changed, CLK,
       comparator_2_eq, comparator_3_eq, comparator_4_eq, comparator_5_eq, comparator_6_eq, Count,
       demultiplexer_3_out0, Idle, Idle_q, Load, Load0, Load1, nand_1_out, or_1_out, or_2_out, or_3_out,
       or_4_out, or_5_out, or_6_out, or_7_out, or_8_out, or_9_out, or_10_out, Proc_q, Update_Mem, Zero_Time;
  wire [3:0] counter_1_q, multiplexer_1_out, subtractor_1_out;
  wire [31:0] register_1_q, register_2_q, register_3_q, register_4_q, register_5_q;

  // Probe on 4'b0011
  // Probe on 4'b0010
  Multiplexer #(.width(4), .enable("false")) multiplexer_1 (
    .in0(4'b0011), .in1(4'b0010), .out(multiplexer_1_out), .sel(nRead_Write));
  or or_1 (or_1_out, Idle, Update_Mem);
  or or_2 (or_2_out, ~Chip_Select, Reset);  // OR_Gate
  Subtractor #(.width(4)) subtractor_1 (.a(multiplexer_1_out), .b(4'b0010), .out(subtractor_1_out));  // open: bin, bout
  Demultiplexer #(.enable("false")) demultiplexer_1 (.out0(Idle), .out1(Load0), .in(Idle_q), .sel(Changed));
  D_Flip_Flop u_Idle (.clk(CLK), .D(or_1_out), .Q(Idle_q), .preset(or_2_out));  // open: Qn, en, reset
  // Probe on counter_1_q
  Counter #(.width(4), .max('hf)) counter_1 (
    .load(Load), .D(subtractor_1_out), .count(Count), .Q(counter_1_q), .clk(CLK), .clr(or_3_out));  // open: carry
  or or_3 (or_3_out, ~Chip_Select, Reset);  // OR_Gate
  Comparator #(.width(4), .mode("unsigned")) comparator_1 (
    .a(4'b0000), .b(counter_1_q), .eq(Zero_Time));  // open: gt, lt
  or or_4 (or_4_out, Count, Load0, Load1);
  Register #(.width(32)) register_1 (.D(Data_In_0), .en(Chip_Select), .Q(register_1_q), .clk(CLK), .clr(or_5_out));
  or or_5 (or_5_out, ~Chip_Select, Reset);  // OR_Gate
  Register #(.width(32)) register_2 (.D(Data_In_1), .en(Chip_Select), .Q(register_2_q), .clk(CLK), .clr(or_6_out));
  or or_6 (or_6_out, ~Chip_Select, Reset);  // OR_Gate
  Register #(.width(32)) register_3 (.D(Data_In_2), .en(Chip_Select), .Q(register_3_q), .clk(CLK), .clr(or_7_out));
  or or_7 (or_7_out, ~Chip_Select, Reset);  // OR_Gate
  Register #(.width(32)) register_4 (.D(Data_In_3), .en(Chip_Select), .Q(register_4_q), .clk(CLK), .clr(or_8_out));
  or or_8 (or_8_out, ~Chip_Select, Reset);  // OR_Gate
  Register #(.width(32)) register_5 (
    .D({{11{1'b1}}, nRead_Write, Mask, Address}), .en(Chip_Select), .Q(register_5_q), .clk(CLK),
    .clr(or_9_out));
  or or_9 (or_9_out, ~Chip_Select, Reset);  // OR_Gate
  D_Flip_Flop Proc (.clk(CLK), .D(or_4_out), .Q(Proc_q), .reset(or_10_out));  // open: Qn, preset, en
  or or_10 (or_10_out, ~Chip_Select, Reset);  // OR_Gate
  Demultiplexer #(.enable("false")) demultiplexer_2 (
    .out0(Count), .out1(Update_Mem), .in(demultiplexer_3_out0), .sel(Zero_Time));
  Demultiplexer #(.enable("false")) demultiplexer_3 (
    .out0(demultiplexer_3_out0), .out1(Load1), .in(Proc_q), .sel(Changed));
  Clock clock_1 (.out(CLK));
  Comparator #(.width(32)) comparator_2 (.a(register_1_q), .b(Data_In_0), .eq(comparator_2_eq));  // open: gt, lt
  Comparator #(.width(32)) comparator_3 (.a(register_2_q), .b(Data_In_1), .eq(comparator_3_eq));  // open: gt, lt
  Comparator #(.width(32)) comparator_4 (.a(register_3_q), .b(Data_In_2), .eq(comparator_4_eq));  // open: gt, lt
  Comparator #(.width(32)) comparator_5 (.a(register_4_q), .b(Data_In_3), .eq(comparator_5_eq));  // open: gt, lt
  Comparator #(.width(32)) comparator_6 (
    .a(register_5_q), .b({{11{1'b1}}, nRead_Write, Mask, Address}), .eq(comparator_6_eq));  // open: gt, lt
  nand nand_1 (nand_1_out, comparator_6_eq, comparator_2_eq, comparator_3_eq, comparator_4_eq, comparator_5_eq);
  and and_1 (Changed, nand_1_out, Chip_Select);
  or or_11 (Load, Count, Load1, Load0);
  and and_2 (and_2_out, Mask[0], Update_Mem, nRead_Write);
  and and_3 (and_3_out, Mask[1], Update_Mem, nRead_Write);
  and and_4 (and_4_out, Mask[2], Update_Mem, nRead_Write);
  and and_5 (and_5_out, Mask[3], Update_Mem, nRead_Write);
  RAM_part #(.addrWidth(16), .dataWidth(32), .bus("separate")) ram_1 (
    .addr(Address), .din(Data_In_0), .data(Data_Out_0), .str(and_2_out), .sel(Chip_Select), .clk(CLK),
    .ld(and_6_out), .clr(Reset));
  and and_6 (and_6_out, ~nRead_Write, Idle);  // AND_Gate
  RAM_part #(.addrWidth(16), .dataWidth(32), .bus("separate")) ram_2 (
    .addr(Address), .din(Data_In_1), .data(Data_Out_1), .str(and_3_out), .sel(Chip_Select), .clk(CLK),
    .ld(and_7_out), .clr(Reset));
  and and_7 (and_7_out, ~nRead_Write, Idle);  // AND_Gate
  RAM_part #(.addrWidth(16), .dataWidth(32), .bus("separate")) ram_3 (
    .addr(Address), .din(Data_In_2), .data(Data_Out_2), .str(and_4_out), .sel(Chip_Select), .clk(CLK),
    .ld(and_8_out), .clr(Reset));
  and and_8 (and_8_out, ~nRead_Write, Idle);  // AND_Gate
  RAM_part #(.addrWidth(16), .dataWidth(32), .bus("separate")) ram_4 (
    .addr(Address), .din(Data_In_3), .data(Data_Out_3), .str(and_5_out), .sel(Chip_Select), .clk(CLK),
    .ld(and_9_out), .clr(Reset));
  and and_9 (and_9_out, ~nRead_Write, Idle);  // AND_Gate

  assign Read_Time = 4'b0011;
  assign Write_Time = 4'b0010;

  // Other names for the same wires on the sheet: M0 = Mask[0]; M1 = Mask[1]; M2 = Mask[2]; M3 = Mask[3];
  //   RW = nRead_Write; CLR = Reset; CS = Chip_Select; Load2 = Count

  // Notes on the sheet:
  //   NO MODIFICAR
  //   excepto quizás los valores RT y WT
  //   BANK0
  //   BANK1
  //   BANK2
  //   BANK3
endmodule

module S_MIPS (
  input  Kbd_Available,
  input  [6:0] Kbd_ASCII_Data,
  input  [31:0] RAM_Out_0,
  input  [31:0] RAM_Out_1,
  input  Reset,
  input  [31:0] RAM_Out_2,
  input  Clock,
  input  [31:0] RAM_Out_3,
  input  [3:0] Read_Time,
  input  [3:0] Write_Time,
  output Kbd_Enable,
  output [15:0] Address,
  output Kbd_Clear,
  output TTY_Enable,
  output [6:0] TTY_ASCII_Data,
  output Stop,
  output [31:0] RAM_In_0,
  output [31:0] RAM_In_1,
  output [31:0] RAM_In_2,
  output [31:0] RAM_In_3,
  output [3:0] Mask,
  output nRead_Write,
  output Chip_Select
);

  wire BANK____0, cu_1_out_14, cu_1_out_16, cu_1_out_19, cu_1_out_20, cu_1_out_21, cu_1_out_23, cu_1_out_25,
       cu_1_out_26, cu_1_out_28, cu_1_out_29, cu_1_out_30, cu_1_out_32, cu_1_out_33, cu_1_out_34,
       cu_1_out_35, cu_1_out_36, data_path_1_out_25, data_path_1_out_26, data_path_1_out_27,
       data_path_1_out_28, data_path_1_out_34, RAM_READ, RAM_WRITE;
  wire [1:0] cu_1_out_15, cu_1_out_17, cu_1_out_24, data_path_1_out_33, RAM_BANK;
  wire [2:0] cu_1_out_37, data_path_1_out_31;
  wire [31:0] ADDR, CURRENT_BANK, RAM_IN;

  Decoder #(.select(2), .disabled(0), .enable("false")) decoder_1 (
    .out0(Mask[0]), .out1(Mask[1]), .out2(Mask[2]), .out3(Mask[3]), .sel(RAM_BANK));
  Multiplexer #(.select(2), .width(32), .disabled(0), .enable("false")) multiplexer_1 (
    .in0(RAM_Out_0), .in1(RAM_Out_1), .in2(RAM_Out_2), .in3(RAM_Out_3), .out(CURRENT_BANK), .sel(RAM_BANK));
  Comparator #(.width(2), .mode("unsigned")) comparator_1 (.a(RAM_BANK), .b(2'b00), .eq(BANK____0));  // open: gt, lt
  MEM_PARSE mem_parse_1 (.IN(ADDR), .BANK(RAM_BANK), .ADDR(Address));
  DELAY delay_1 (.TIME(Read_Time), .Q(RAM_READ), .CLK(Clock), .RST(Reset));
  DELAY delay_2 (.TIME(Write_Time), .Q(RAM_WRITE), .CLK(Clock), .RST(Reset));
  Demultiplexer #(.select(2), .width(32), .enable("false")) demultiplexer_1 (
    .out0(RAM_In_0), .out1(RAM_In_1), .out2(RAM_In_2), .out3(RAM_In_3), .in(RAM_IN), .sel(RAM_BANK));
  CU cu_1 (
    .out_14(cu_1_out_14), .out_15(cu_1_out_15), .in_1(Clock), .in_2(data_path_1_out_25),
    .out_16(cu_1_out_16), .out_17(cu_1_out_17), .in_3(Reset), .out_19(cu_1_out_19), .out_20(cu_1_out_20),
    .out_21(cu_1_out_21), .in_4(RAM_READ), .in_5(data_path_1_out_26), .out_23(cu_1_out_23),
    .out_24(cu_1_out_24), .in_6(RAM_WRITE), .out_25(cu_1_out_25), .out_26(cu_1_out_26),
    .in_8(data_path_1_out_31), .in_9(data_path_1_out_28), .out_28(cu_1_out_28), .out_29(cu_1_out_29),
    .out_30(cu_1_out_30), .in_10(data_path_1_out_33), .in_11(Kbd_Available), .out_32(cu_1_out_32),
    .out_33(cu_1_out_33), .in_12(data_path_1_out_34), .in_13(Stop), .out_34(cu_1_out_34),
    .out_35(cu_1_out_35), .out_36(cu_1_out_36), .in_7(data_path_1_out_27), .out_18(TTY_Enable),
    .out_22(Kbd_Enable), .out_31(Chip_Select), .out_27(nRead_Write), .out_37(cu_1_out_37));
  DATA_PATH data_path_1 (
    .out_25(data_path_1_out_25), .in_1(cu_1_out_14), .CURRENT_BANK(CURRENT_BANK), .in_3(cu_1_out_16),
    .in_4(cu_1_out_19), .out_26(data_path_1_out_26), .CLR(Reset), .in_6(cu_1_out_21), .CLK(Clock),
    .out_27(data_path_1_out_27), .in_8(cu_1_out_23), .in_9(cu_1_out_25), .out_28(data_path_1_out_28),
    .in_10(cu_1_out_29), .in_11(cu_1_out_15), .in_12(cu_1_out_28), .out_30(Stop), .in_13(cu_1_out_33),
    .in_14(cu_1_out_17), .in_15(cu_1_out_30), .out_31(data_path_1_out_31), .in_16(cu_1_out_32),
    .in_17(Kbd_ASCII_Data), .in_18(cu_1_out_20), .in_19(cu_1_out_34), .out_33(data_path_1_out_33),
    .in_20(cu_1_out_35), .in_21(cu_1_out_24), .in_22(cu_1_out_36), .out_34(data_path_1_out_34),
    .in_23(cu_1_out_26), .out_29(TTY_ASCII_Data), .out_32(ADDR), .out_35(RAM_IN), .in_24(cu_1_out_37));

  // Other names for the same wires on the sheet: CLK = Clock; CLR = Reset; CS = Chip_Select;
  //   KBD_AVAIL = Kbd_Available; KBD_CLR = Kbd_Clear; KBD_DATA[6:0] = Kbd_ASCII_Data; RAM_A[15:0] = Address;
  //   RAM_INPUT_0[31:0] = RAM_In_0; RAM_INPUT_1[31:0] = RAM_In_1; RAM_INPUT_2[31:0] = RAM_In_2;
  //   RAM_INPUT_3[31:0] = RAM_In_3; RAM_MASK[3:0] = Mask; RAM_OUTPUT_0[31:0] = RAM_Out_0;
  //   RAM_OUTPUT_1[31:0] = RAM_Out_1; RAM_OUTPUT_2[31:0] = RAM_Out_2; RAM_OUTPUT_3[31:0] = RAM_Out_3;
  //   RW = nRead_Write; TTY_DATA[6:0] = TTY_ASCII_Data

  // Notes on the sheet:
  //   RAM ADDRESS
  //   DATA FROM RAM
  //   DATA TO RAM
  //   DATA WRITE MASK
  //   RAM TIMING
  //   RAM CONTROL
  //   KEYBOARD
  //   TTY
  //   SEQUENCING
endmodule

module RAM_Dispatcher (
  input  [3:0] WriteTime,
  input  Clock,
  input  CLR,
  output [31:0] Data,
  output [15:0] Address,
  output [3:0] Mask,
  output Finished,
  output Write
);

  wire demultiplexer_2_out1, demultiplexer_3_out1, End, IDLE_q, IncAddr, Load, or_1_out, or_2_out, While_q,
       WriteEnd;
  wire [3:0] counter_1_q;
  wire [31:0] CurrentAddress_q;

  Counter #(.width(32), .max('hffffffff)) CurrentAddress (
    .count(IncAddr), .Q({CurrentAddress_q[31:18], Address, CurrentAddress_q[1:0]}), .clk(Clock), .clr(CLR));  // open: load, D, carry
  or or_1 (or_1_out, IncAddr, demultiplexer_3_out1, Finished);
  D_Flip_Flop IDLE (.clk(Clock), .D(or_1_out), .Q(IDLE_q), .preset(CLR));  // open: Qn, en, reset
  Demultiplexer #(.enable("false")) demultiplexer_1 (.out0(Load), .out1(Finished), .in(IDLE_q), .sel(End));
  D_Flip_Flop While (.clk(Clock), .D(or_2_out), .Q(While_q), .reset(CLR));  // open: Qn, preset, en
  or or_2 (or_2_out, Write, Load);
  RAM_part #(.addrWidth(18), .dataWidth(32)) ram_1 (
    .addr({Address, CurrentAddress_q[1:0]}), .data(Data), .clk(Clock));  // open: sel, ld, clr
  Demultiplexer #(.enable("false")) demultiplexer_2 (
    .out0(Write), .out1(demultiplexer_2_out1), .in(While_q), .sel(WriteEnd));
  Decoder #(.select(2)) decoder_1 (
    .out0(Mask[0]), .out1(Mask[1]), .out2(Mask[2]), .out3(Mask[3]), .sel(CurrentAddress_q[1:0]));  // open: en
  Demultiplexer #(.enable("false")) demultiplexer_3 (
    .out0(IncAddr), .out1(demultiplexer_3_out1), .in(demultiplexer_2_out1), .sel(End));
  Counter #(.width(4), .max('hf)) counter_1 (
    .load(Load), .D(WriteTime), .count(Write), .Q(counter_1_q), .clk(Clock));  // open: carry, clr
  Comparator #(.width(32)) comparator_1 (.a(Data), .b({32{1'b1}}), .eq(End));  // open: gt, lt
  Comparator #(.width(4)) comparator_2 (.a(4'b0000), .b(counter_1_q), .eq(WriteEnd));  // open: gt, lt

  // Other names for the same wires on the sheet: CLK = Clock; Count = Write; WT[3:0] = WriteTime
endmodule

module RF (
  input  WRITE,
  input  [31:0] IN,
  input  [4:0] SEL,
  input  CLK,
  input  RST,
  input  [31:0] SP_IN,
  output [31:0] OUT,
  output [31:0] SP_OUT
);

  wire and_1_out, comparator_1_eq, R1I, R2I, R3I, R4I, R5I, R6I, R7I, R8I, R9I, R10I, R11I, R12I, R13I, R14I,
       R15I, R16I, R17I, R18I, R19I, R20I, R21I, R22I, R23I, R24I, R25I, R26I, R27I, R28I, R29I, R30I,
       undriven;
  wire [31:0] R1O, R2O, R3O, R4O, R5O, R6O, R7O, R8O, R9O, R10O, R11O, R12O, R13O, R14O, R15O, R16O, R17O,
       R18O, R19O, R20O, R21O, R22O, R23O, R24O, R25O, R26O, R27O, R28O, R29O, R30O, R31I;

  Comparator #(.width(5), .mode("unsigned")) comparator_1 (
    .a({5{1'b1}}), .b(SEL), .eq(comparator_1_eq));  // open: gt, lt
  Multiplexer #(.width(32), .enable("false")) multiplexer_1 (.in0(SP_IN), .in1(IN), .out(R31I), .sel(and_1_out));
  and and_1 (and_1_out, comparator_1_eq, WRITE);
  Register #(.width(32)) R4 (.D(IN), .en(R4I), .Q(R4O), .clk(CLK), .clr(RST));
  Register #(.width(32)) R1 (.D(IN), .en(R1I), .Q(R1O), .clk(CLK), .clr(RST));
  Register #(.width(32)) R5 (.D(IN), .en(R5I), .Q(R5O), .clk(CLK), .clr(RST));
  Decoder #(.select(5), .disabled(0)) decoder_1 (
    .out1(R1I), .out2(R2I), .out3(R3I), .out4(R4I), .out5(R5I), .out6(R6I), .out7(R7I), .out8(R8I),
    .out9(R9I), .out10(R10I), .out11(R11I), .out12(R12I), .out13(R13I), .out14(R14I), .out15(R15I),
    .out16(R16I), .out17(R17I), .out18(R18I), .out19(R19I), .out20(R20I), .out21(R21I), .out22(R22I),
    .out23(R23I), .out24(R24I), .out25(R25I), .out26(R26I), .out27(R27I), .out28(R28I), .out29(R29I),
    .out30(R30I), .sel(SEL), .en(WRITE));  // open: out0, out31
  Register #(.width(32)) R3 (.D(IN), .en(R3I), .Q(R3O), .clk(CLK), .clr(RST));
  Register #(.width(32)) R2 (.D(IN), .en(R2I), .Q(R2O), .clk(CLK), .clr(RST));
  Register #(.width(32)) R7 (.D(IN), .en(R7I), .Q(R7O), .clk(CLK), .clr(RST));
  Register #(.width(32)) R6 (.D(IN), .en(R6I), .Q(R6O), .clk(CLK), .clr(RST));
  Register #(.width(32)) R8 (.D(IN), .en(R8I), .Q(R8O), .clk(CLK), .clr(RST));
  Register #(.width(32)) R12 (.D(IN), .en(R12I), .Q(R12O), .clk(CLK), .clr(RST));
  Register #(.width(32)) R9 (.D(IN), .en(R9I), .Q(R9O), .clk(CLK), .clr(RST));
  Register #(.width(32)) R13 (.D(IN), .en(R13I), .Q(R13O), .clk(CLK), .clr(RST));
  Register #(.width(32)) R10 (.D(IN), .en(R10I), .Q(R10O), .clk(CLK), .clr(RST));
  Register #(.width(32)) R14 (.D(IN), .en(R14I), .Q(R14O), .clk(CLK), .clr(RST));
  Register #(.width(32)) R11 (.D(IN), .en(R11I), .Q(R11O), .clk(CLK), .clr(RST));
  Register #(.width(32)) R15 (.D(IN), .en(R15I), .Q(R15O), .clk(CLK), .clr(RST));
  Register #(.width(32)) R16 (.D(IN), .en(R16I), .Q(R16O), .clk(CLK), .clr(RST));
  Register #(.width(32)) _20R (.D(IN), .en(undriven), .Q(R20O), .clk(CLK), .clr(RST));
  Register #(.width(32)) R17 (.D(IN), .en(R17I), .Q(R17O), .clk(CLK), .clr(RST));
  Register #(.width(32)) R21 (.D(IN), .en(R21I), .Q(R21O), .clk(CLK), .clr(RST));
  Register #(.width(32)) R18 (.D(IN), .en(R18I), .Q(R18O), .clk(CLK), .clr(RST));
  Register #(.width(32)) R22 (.D(IN), .en(R22I), .Q(R22O), .clk(CLK), .clr(RST));
  Register #(.width(32)) R19 (.D(IN), .en(R19I), .Q(R19O), .clk(CLK), .clr(RST));
  Register #(.width(32)) R23 (.D(IN), .en(R23I), .Q(R23O), .clk(CLK), .clr(RST));
  Register #(.width(32)) R24 (.D(IN), .en(R24I), .Q(R24O), .clk(CLK));  // open: clr
  Register #(.width(32)) R25 (.D(IN), .en(R25I), .Q(R25O), .clk(CLK));  // open: clr
  Register #(.width(32)) R28 (.D(IN), .en(R28I), .Q(R28O), .clk(CLK));  // open: clr
  Register #(.width(32)) R29 (.D(IN), .en(R29I), .Q(R29O), .clk(CLK));  // open: clr
  Register #(.width(32)) R26 (.D(IN), .en(R26I), .Q(R26O), .clk(CLK));  // open: clr
  Register #(.width(32)) R30 (.D(IN), .en(R30I), .Q(R30O), .clk(CLK));  // open: clr
  Register #(.width(32)) R27 (.D(IN), .en(R27I), .Q(R27O), .clk(CLK));  // open: clr
  Register #(.width(32)) R31 (.D(R31I), .Q(SP_OUT), .clk(CLK));  // open: en, clr
  Multiplexer #(.select(5), .width(32), .enable("false")) multiplexer_2 (
    .in0({32{1'b0}}), .in1(R1O), .in2(R2O), .in3(R3O), .in4(R4O), .in5(R5O), .in6(R6O), .in7(R7O), .in8(R8O),
    .in9(R9O), .in10(R10O), .in11(R11O), .in12(R12O), .in13(R13O), .in14(R14O), .in15(R15O), .in16(R16O),
    .in17(R17O), .in18(R18O), .in19(R19O), .in20(R20O), .in21(R21O), .in22(R22O), .in23(R23O), .in24(R24O),
    .in25(R25O), .in26(R26O), .in27(R27O), .in28(R28O), .in29(R29O), .in30(R30O), .in31(SP_OUT), .out(OUT),
    .sel(SEL));

  // Other names for the same wires on the sheet: INPUT[31:0] = IN; R31O[31:0] = SP_OUT; RESET = RST;
  //   SP_IN_t[31:0] = R31I; W = WRITE
endmodule

module ALU (
  input  [31:0] IN_A,
  input  [31:0] IN_B,
  input  U,
  input  [2:0] SEL,
  output [31:0] OUT1,
  output [31:0] OUT2,
  output out_7,
  output out_8,
  output out_9
);

  wire abs_1_sf, abs_2_sf, decoder_1_out0, decoder_1_out1, xor_1_out;
  wire [2:0] comparator_1_gt, comparator_2_gt;
  wire [31:0] abs_1_out, abs_2_out, ADD_OUT, AND_OUT, DIV_OUT1, DIV_OUT_2, divider_2_out, MUL_OUT1,
       MUL_OUT_2, multiplexer_5_out, multiplexer_6_out, multiplexer_7_out, multiplexer_8_out,
       multiplier_2_cout, multiplier_2_out, neg_64_1_out_a, neg_64_1_out_b, negator_1_out, NOR_OUT, OR_OUT,
       SUB_OUT, U_DIV_OUT1, U_DIV_OUT_2, U_MUL_OUT1, U_MUL_OUT_2, XOR_OUT;

  Adder #(.width(32)) adder_1 (.a(IN_A), .b(IN_B), .out(ADD_OUT));  // open: cin, cout
  Subtractor #(.width(32)) subtractor_1 (.a(IN_A), .b(IN_B), .out(SUB_OUT));  // open: bin, bout
  Multiplier #(.width(32)) multiplier_1 (.a(IN_A), .b(IN_B), .out(U_MUL_OUT1), .cout(U_MUL_OUT_2));  // open: cin
  Divider #(.width(32)) divider_1 (.a(IN_A), .b(IN_B), .out(U_DIV_OUT1), .rem(U_DIV_OUT_2));  // open: upper
  ABS abs_1 (.IN(IN_A), .OUT(abs_1_out), .SF(abs_1_sf));
  ABS abs_2 (.IN(IN_B), .OUT(abs_2_out), .SF(abs_2_sf));
  xor xor_1 (xor_1_out, abs_2_sf, abs_1_sf);
  Multiplier #(.width(32)) multiplier_2 (
    .a(abs_1_out), .b(abs_2_out), .out(multiplier_2_out), .cout(multiplier_2_cout));  // open: cin
  Divider #(.width(32)) divider_2 (.a(abs_2_out), .b(abs_1_out), .out(divider_2_out), .rem(DIV_OUT_2));  // open: upper
  Negator #(.width(32)) negator_1 (.in(divider_2_out), .out(negator_1_out));
  assign AND_OUT = IN_A & IN_B;  // AND_Gate and_1, 32 bits wide
  assign OR_OUT = IN_A | IN_B;  // OR_Gate or_1, 32 bits wide
  assign XOR_OUT = IN_A ^ IN_B;  // XOR_Gate xor_2, 32 bits wide
  NEG_64 neg_64_1 (.IN_A(multiplier_2_cout), .IN_B(multiplier_2_out), .OUT_A(neg_64_1_out_a), .OUT_B(neg_64_1_out_b));
  Multiplexer #(.width(32), .enable("false")) multiplexer_1 (
    .in0(divider_2_out), .in1(negator_1_out), .out(DIV_OUT1), .sel(xor_1_out));
  assign NOR_OUT = ~OR_OUT;  // NOT_Gate not_1, 32 bits wide
  Multiplexer #(.width(32), .enable("false")) multiplexer_2 (
    .in0(multiplier_2_cout), .in1(neg_64_1_out_a), .out(MUL_OUT_2), .sel(xor_1_out));
  Multiplexer #(.width(32), .enable("false")) multiplexer_3 (
    .in0(multiplier_2_out), .in1(neg_64_1_out_b), .out(MUL_OUT1), .sel(xor_1_out));
  Comparator #(.width(32)) comparator_1 (
    .a(IN_A), .b(IN_B), .gt(comparator_1_gt[0]), .eq(comparator_1_gt[1]), .lt(comparator_1_gt[2]));
  Comparator #(.width(32), .mode("unsigned")) comparator_2 (
    .a(IN_A), .b(IN_B), .gt(comparator_2_gt[0]), .eq(comparator_2_gt[1]), .lt(comparator_2_gt[2]));
  Multiplexer #(.width(3), .enable("false")) multiplexer_4 (
    .in0(comparator_1_gt), .in1(comparator_2_gt), .out({out_9, out_8, out_7}), .sel(U));
  Multiplexer #(.width(32), .enable("false")) multiplexer_5 (
    .in0(MUL_OUT1), .in1(U_MUL_OUT1), .out(multiplexer_5_out), .sel(U));
  Multiplexer #(.width(32), .enable("false")) multiplexer_6 (
    .in0(DIV_OUT1), .in1(U_DIV_OUT1), .out(multiplexer_6_out), .sel(U));
  Multiplexer #(.width(32), .enable("false")) multiplexer_7 (
    .in0(DIV_OUT_2), .in1(U_DIV_OUT_2), .out(multiplexer_7_out), .sel(U));
  Multiplexer #(.width(32), .enable("false")) multiplexer_8 (
    .in0(MUL_OUT_2), .in1(U_MUL_OUT_2), .out(multiplexer_8_out), .sel(U));
  Decoder #(.enable("false")) decoder_1 (.out0(decoder_1_out0), .out1(decoder_1_out1), .sel(SEL[2]));
  Multiplexer #(.select(2), .width(32)) multiplexer_9 (
    .in0(ADD_OUT), .in1(SUB_OUT), .in2(multiplexer_5_out), .in3(multiplexer_6_out), .out(OUT1),
    .sel(SEL[1:0]), .en(decoder_1_out0));
  Multiplexer #(.width(32)) multiplexer_10 (
    .in0(multiplexer_8_out), .in1(multiplexer_7_out), .out(OUT2), .sel(SEL[0]), .en(decoder_1_out0));
  Multiplexer #(.select(2), .width(32)) multiplexer_11 (
    .in0(AND_OUT), .in1(OR_OUT), .in2(NOR_OUT), .in3(XOR_OUT), .out(OUT1), .sel(SEL[1:0]), .en(decoder_1_out1));

  // Other names for the same wires on the sheet: GR = out_7; EQ = out_8; LS = out_9
endmodule

module ID (
  input  [31:0] INSTRUCTION,
  input  EN,
  output [2:0] OP,
  output [1:0] OP_TYPE,
  output I,
  output U,
  output [4:0] out_7,
  output [4:0] out_8,
  output [4:0] out_9,
  output [25:0] out_10,
  output [15:0] out_11
);

  wire ADD, ADD0, ADD1, AND, AND0, AND1, BEQ, BGTZ, BLEZ, BLTZ, BNE, comparator_1_eq, comparator_2_eq,
       comparator_3_eq, comparator_4_eq, comparator_5_eq, comparator_6_eq, comparator_7_eq, comparator_10_eq,
       comparator_11_eq, comparator_12_eq, comparator_13_eq, comparator_14_eq, comparator_15_eq,
       comparator_16_eq, comparator_17_eq, comparator_18_eq, comparator_19_eq, comparator_23_eq,
       comparator_24_eq, comparator_25_eq, comparator_26_eq, comparator_27_eq, comparator_28_eq,
       comparator_29_eq, DIV, DIVU, HALT, JMP, JMPR, KBD, LW, MFHI, MFLO, MUL, MULU, NOP, NOR, OP0, OP1, OP2,
       OP3, OP4, OP5, OP6, OP7, OPC_0, OPT0, OPT1, OPT2, OPT3, OR, OR0, OR1, or_1_out, or_2_out, or_3_out,
       POP, PUSH, RND, SLT, SLT0, SLT1, SLTU, SLTU0, SUB, SW, TTY, XOR0, XOR1;
  wire [5:0] FUNC___1;
  wire [31:26] INS;

  BYTE_REV byte_rev_1 (.IN(INSTRUCTION), .OUT({INS, out_7, out_8, out_9, out_10[10:0]}));
  Priority_Encoder #(.select(2)) priority_encoder_1 (
    .in0(OPT0), .in1(OPT1), .in2(OPT2), .in3(OPT3), .out(OP_TYPE), .en_in(EN));  // open: gs, en_out
  Priority_Encoder priority_encoder_2 (
    .in0(OP0), .in1(OP1), .in2(OP2), .in3(OP3), .in4(OP4), .in5(OP5), .in6(OP6), .in7(OP7), .out(OP),
    .en_in(EN));  // open: gs, en_out
  Comparator #(.width(6), .mode("unsigned")) comparator_1 (
    .a(INS), .b({6{1'b1}}), .eq(comparator_1_eq));  // open: gt, lt
  Comparator #(.width(6), .mode("unsigned")) comparator_2 (
    .a(out_10[5:0]), .b({6{1'b1}}), .eq(comparator_2_eq));  // open: gt, lt
  Comparator #(.width(6), .mode("unsigned")) comparator_3 (
    .a(out_10[5:0]), .b(6'b000001), .eq(comparator_3_eq));  // open: gt, lt
  Comparator #(.width(6), .mode("unsigned")) comparator_4 (
    .a(out_10[5:0]), .b(6'b000010), .eq(comparator_4_eq));  // open: gt, lt
  Comparator #(.width(6), .mode("unsigned")) comparator_5 (
    .a(out_10[5:0]), .b(6'b000100), .eq(comparator_5_eq));  // open: gt, lt
  and and_1 (HALT, comparator_1_eq, comparator_2_eq);
  and and_2 (TTY, comparator_1_eq, comparator_3_eq);
  and and_3 (RND, comparator_1_eq, comparator_4_eq);
  and and_4 (KBD, comparator_1_eq, comparator_5_eq);
  Subtractor #(.width(6)) subtractor_1 (.a(out_10[5:0]), .b(6'b000001), .out(FUNC___1));  // open: bin, bout
  Comparator #(.width(6), .mode("unsigned")) comparator_6 (
    .a(out_10[5:0]), .b(6'b010000), .eq(comparator_6_eq));  // open: gt, lt
  Comparator #(.width(6), .mode("unsigned")) comparator_7 (
    .a(out_10[5:0]), .b(6'b001000), .eq(comparator_7_eq));  // open: gt, lt
  Comparator #(.width(6), .mode("unsigned")) comparator_8 (.a(INS), .b(6'b000010), .eq(JMP));  // open: gt, lt
  Comparator #(.width(6), .mode("unsigned")) comparator_9 (.a(INS), .b({6{1'b0}}), .eq(OPC_0));  // open: gt, lt
  Comparator #(.width(6), .mode("unsigned")) comparator_10 (
    .a(out_10[5:0]), .b({6{1'b0}}), .eq(comparator_10_eq));  // open: gt, lt
  Comparator #(.width(6), .mode("unsigned")) comparator_11 (
    .a(out_10[5:0]), .b(6'b100000), .eq(comparator_11_eq));  // open: gt, lt
  Comparator #(.width(6), .mode("unsigned")) comparator_12 (
    .a(out_10[5:0]), .b(6'b100010), .eq(comparator_12_eq));  // open: gt, lt
  Comparator #(.width(6), .mode("unsigned")) comparator_13 (
    .a(out_10[5:0]), .b(6'b011000), .eq(comparator_13_eq));  // open: gt, lt
  or or_1 (or_1_out, comparator_13_eq, comparator_14_eq);
  Comparator #(.width(6), .mode("unsigned")) comparator_14 (
    .a(FUNC___1), .b(6'b011000), .eq(comparator_14_eq));  // open: gt, lt
  Comparator #(.width(6), .mode("unsigned")) comparator_15 (
    .a(out_10[5:0]), .b(6'b011010), .eq(comparator_15_eq));  // open: gt, lt
  or or_2 (or_2_out, comparator_15_eq, comparator_16_eq);
  Comparator #(.width(6), .mode("unsigned")) comparator_16 (
    .a(FUNC___1), .b(6'b011010), .eq(comparator_16_eq));  // open: gt, lt
  Comparator #(.width(6), .mode("unsigned")) comparator_17 (
    .a(out_10[5:0]), .b(6'b101010), .eq(comparator_17_eq));  // open: gt, lt
  or or_3 (or_3_out, comparator_17_eq, comparator_18_eq);
  Comparator #(.width(6), .mode("unsigned")) comparator_18 (
    .a(FUNC___1), .b(6'b101010), .eq(comparator_18_eq));  // open: gt, lt
  and and_5 (MFHI, OPC_0, comparator_6_eq);
  and and_6 (JMPR, OPC_0, comparator_7_eq);
  and and_7 (NOP, OPC_0, comparator_10_eq);
  and and_8 (ADD0, OPC_0, comparator_11_eq);
  and and_9 (SUB, OPC_0, comparator_12_eq);
  and and_10 (MUL, OPC_0, or_1_out);
  and and_11 (MULU, MUL, comparator_14_eq);
  and and_12 (DIV, OPC_0, or_2_out);
  and and_13 (DIVU, DIV, comparator_16_eq);
  and and_14 (SLT0, OPC_0, or_3_out);
  and and_15 (SLTU0, SLT0, comparator_18_eq);
  or or_4 (OPT0, ADD, SUB, MUL, DIV, AND, OR, NOR, OP7);
  Comparator #(.width(6), .mode("unsigned")) comparator_19 (
    .a(out_10[5:0]), .b(6'b010010), .eq(comparator_19_eq));  // open: gt, lt
  Comparator #(.width(6), .mode("unsigned")) comparator_20 (.a(INS), .b(6'b000001), .eq(BLTZ));  // open: gt, lt
  Comparator #(.width(6), .mode("unsigned")) comparator_21 (.a(INS), .b(6'b000111), .eq(BGTZ));  // open: gt, lt
  Comparator #(.width(6), .mode("unsigned")) comparator_22 (.a(INS), .b(6'b000110), .eq(BLEZ));  // open: gt, lt
  or or_5 (OP0, ADD, SLT, BEQ, NOP);
  or or_6 (OP2, MUL, SW, BLEZ, TTY);
  or or_7 (OP4, AND, PUSH, BLTZ, KBD);
  Comparator #(.width(6), .mode("unsigned")) comparator_23 (
    .a(out_10[5:0]), .b(6'b100100), .eq(comparator_23_eq));  // open: gt, lt
  Comparator #(.width(6), .mode("unsigned")) comparator_24 (
    .a(out_10[5:0]), .b(6'b100101), .eq(comparator_24_eq));  // open: gt, lt
  and and_16 (MFLO, OPC_0, comparator_19_eq);
  or or_8 (OPT1, SLT, LW, SW, POP, PUSH, MFHI, MFLO);
  and and_17 (AND0, OPC_0, comparator_23_eq);
  and and_18 (OR0, OPC_0, comparator_24_eq);
  or or_9 (OP1, SUB, LW, BNE, HALT);
  or or_10 (OP3, DIV, POP, BGTZ, RND);
  or or_11 (OP5, OR, MFHI, JMP);
  Comparator #(.width(6), .mode("unsigned")) comparator_25 (
    .a(out_10[5:0]), .b(6'b100111), .eq(comparator_25_eq));  // open: gt, lt
  Comparator #(.width(6), .mode("unsigned")) comparator_26 (
    .a(out_10[5:0]), .b(6'b101000), .eq(comparator_26_eq));  // open: gt, lt
  Comparator #(.width(6), .mode("unsigned")) comparator_27 (
    .a(INS), .b(6'b111000), .eq(comparator_27_eq));  // open: gt, lt
  Comparator #(.width(6), .mode("unsigned")) comparator_28 (
    .a(out_10[5:0]), .b({6{1'b0}}), .eq(comparator_28_eq));  // open: gt, lt
  Comparator #(.width(6), .mode("unsigned")) comparator_29 (
    .a(FUNC___1), .b({6{1'b0}}), .eq(comparator_29_eq));  // open: gt, lt
  Comparator #(.width(6), .mode("unsigned")) comparator_30 (.a(INS), .b(6'b100011), .eq(LW));  // open: gt, lt
  or or_12 (OP6, NOR, MFLO, JMPR);
  or or_13 (OPT2, BEQ, BNE, BLEZ, BGTZ, BLTZ, JMP, JMPR);
  and and_19 (NOR, OPC_0, comparator_25_eq);
  and and_20 (XOR0, OPC_0, comparator_26_eq);
  and and_21 (POP, comparator_27_eq, comparator_28_eq);
  and and_22 (PUSH, comparator_27_eq, comparator_29_eq);
  or or_14 (I, ADD1, SLT1, AND1, OR1, XOR1);
  or or_15 (U, MULU, DIVU, SLTU);
  or or_16 (OR, OR0, OR1);
  Comparator #(.width(6), .mode("unsigned")) comparator_31 (.a(INS), .b(6'b101011), .eq(SW));  // open: gt, lt
  or or_17 (OPT3, NOP, HALT, TTY, RND, KBD);
  Comparator #(.width(6), .mode("unsigned")) comparator_32 (.a(INS), .b(6'b001000), .eq(ADD1));  // open: gt, lt
  Comparator #(.width(6), .mode("unsigned")) comparator_33 (.a(INS), .b(6'b001010), .eq(SLT1));  // open: gt, lt
  Comparator #(.width(6), .mode("unsigned")) comparator_34 (.a(INS), .b(6'b000100), .eq(BEQ));  // open: gt, lt
  Comparator #(.width(6), .mode("unsigned")) comparator_35 (.a(INS), .b(6'b000101), .eq(BNE));  // open: gt, lt
  or or_18 (AND, AND0, AND1);
  or or_19 (SLT, SLT0, SLT1);
  or or_20 (SLTU, SLTU0, SLT1);
  or or_21 (OP7, XOR0, XOR1);
  or or_22 (ADD, ADD0, ADD1);
  Comparator #(.width(6), .mode("unsigned")) comparator_36 (.a(INS), .b(6'b001100), .eq(AND1));  // open: gt, lt
  Comparator #(.width(6), .mode("unsigned")) comparator_37 (.a(INS), .b(6'b001101), .eq(OR1));  // open: gt, lt
  Comparator #(.width(6), .mode("unsigned")) comparator_38 (.a(INS), .b(6'b001110), .eq(XOR1));  // open: gt, lt

  assign out_10[25:11] = {out_7, out_8, out_9};
  assign out_11 = {out_9, out_10[10:0]};

  // Other names for the same wires on the sheet: ADDI = ADD1; ANDI = AND1; ENABLED = EN; IMDT = I;
  //   CONST[15:0] = {out_9, out_10[10:0]}; INS[25:0] = {out_7, out_8, out_9, out_10[10:0]};
  //   JUMP_DEST[25:0] = {out_7, out_8, out_9, out_10[10:0]}; R_FUNC_CODE[5:0] = out_10[5:0]; ARG_3[4:0] = out_9;
  //   ARG_2[4:0] = out_8; ARG_1[4:0] = out_7; OPCODE[5:0] = INS; ORI = OR1; SLTI = SLT1; SLTU1 = SLT1; UNSIGNED = U;
  //   XOR = OP7; XORI = XOR1

  // Notes on the sheet:
  //   0 - Arithmetic & Logic
  //   1 - Memory
  //   2 - Flow Control
  //   3 - Specials
endmodule

module DELAY (
  input  [3:0] TIME,
  input  CLK,
  input  RST,
  output Q
);

  wire comparator_1_eq, or_1_out;
  wire [3:0] counter_1_q;

  Counter #(.width(4), .max('hf)) counter_1 (
    .Q(counter_1_q), .clk(CLK), .clr(or_1_out));  // open: load, D, count, carry
  or or_1 (or_1_out, comparator_1_eq, RST);
  Comparator #(.width(4), .mode("unsigned")) comparator_1 (
    .a(TIME), .b(counter_1_q), .eq(comparator_1_eq));  // open: gt, lt
  D_Flip_Flop d_ff_1 (.clk(CLK), .D(comparator_1_eq), .Q(Q), .preset(comparator_1_eq), .reset(RST));  // open: Qn, en
endmodule

module MEM_PARSE (
  input  [31:0] IN,
  output [1:0] BANK,
  output [15:0] ADDR
);


  assign ADDR = IN[19:4];
  assign BANK = IN[3:2];
endmodule

module ABS (
  input  [31:0] IN,
  output [31:0] OUT,
  output SF
);

  wire [31:0] negator_1_out;

  Multiplexer #(.width(32), .enable("false")) multiplexer_1 (.in0(IN), .in1(negator_1_out), .out(OUT), .sel(IN[31]));
  Negator #(.width(32)) negator_1 (.in(IN), .out(negator_1_out));

  assign SF = IN[31];
endmodule

module NEG_64 (
  input  [31:0] IN_A,
  input  [31:0] IN_B,
  output [31:0] OUT_A,
  output [31:0] OUT_B
);

  wire adder_1_cout;
  wire [31:0] not_1_out, not_2_out;

  assign not_1_out = ~IN_B;  // NOT_Gate not_1, 32 bits wide
  Adder #(.width(32)) adder_1 (.a(not_1_out), .b(32'h1), .out(OUT_B), .cout(adder_1_cout));  // open: cin
  assign not_2_out = ~IN_A;  // NOT_Gate not_2, 32 bits wide
  Adder #(.width(32)) adder_2 (.a(not_2_out), .b({32{1'b0}}), .out(OUT_A), .cin(adder_1_cout));  // open: cout
endmodule

module BYTE_REV (
  input  [31:0] IN,
  output [31:0] OUT
);


  assign OUT = {IN[7:0], IN[15:8], IN[23:16], IN[31:24]};
endmodule

module CU (
  input  in_1,
  input  in_2,
  input  in_3,
  input  in_4,
  input  in_5,
  input  in_6,
  input  in_7,
  input  [2:0] in_8,
  input  in_9,
  input  [1:0] in_10,
  input  in_11,
  input  in_12,
  input  in_13,
  output out_14,
  output [1:0] out_15,
  output out_16,
  output [1:0] out_17,
  output out_18,
  output out_19,
  output out_20,
  output out_21,
  output out_22,
  output out_23,
  output [1:0] out_24,
  output out_25,
  output out_26,
  output out_27,
  output out_28,
  output out_29,
  output out_30,
  output out_31,
  output out_32,
  output out_33,
  output out_34,
  output out_35,
  output out_36,
  output [2:0] out_37
);

  wire A1____A2, ADR10, ADR11, BEQ, BGTZ, BLEZ, BLTZ, BNE, BRANCH, BRANCH0, BRANCH1, BRANCH2, BRANCH3,
       BRANCH4, CHANGE_TR_3_q, CS0, CS1, CS2, CS3, CS4, demultiplexer_1_out0, demultiplexer_1_out1,
       demultiplexer_1_out2, demultiplexer_1_out3, demultiplexer_1_out4, demultiplexer_1_out5,
       demultiplexer_1_out6, demultiplexer_1_out7, demultiplexer_3_out0, demultiplexer_3_out1,
       demultiplexer_4_out0, demultiplexer_5_out0, demultiplexer_6_out0, demultiplexer_9_out0,
       demultiplexer_10_out0, demultiplexer_11_out0, demultiplexer_11_out1, demultiplexer_12_out0,
       demultiplexer_12_out1, demultiplexer_13_out0, demultiplexer_13_out1, demultiplexer_14_out0,
       demultiplexer_16_out1, demultiplexer_17_out0, demultiplexer_17_out1, demultiplexer_19_out0,
       demultiplexer_19_out1, IDLE_q, J, JR, L_A_0, L_TR_0, L_TR_2, L_TR_4, L_TR_5, L_TR_6, LHALT0, LOAD_q,
       LOAD_RAM_2_q, LOAD_RAM_3_q, LOAD_RAM_q, LPC0, LPC2, LRAM1, MFHI, MFLO, OPT0, OPT1, OPT2, OPT3,
       or_1_out, or_3_out, or_4_out, or_5_out, or_8_out, or_11_out, or_12_out, or_16_out, or_22_out,
       or_23_out, or_24_out, REG00, REG02, REG10, REGW0, Set_ADDR_q, TO_IDLE, TR_1_0, TR_1_5, WE0, WE1, WE2,
       WE4, WE5, WE6, WE7, WHILE_END, While_q;

  Demultiplexer #(.select(3), .enable("false")) demultiplexer_1 (
    .out0(demultiplexer_1_out0), .out1(demultiplexer_1_out1), .out2(demultiplexer_1_out2),
    .out3(demultiplexer_1_out3), .out4(demultiplexer_1_out4), .out5(demultiplexer_1_out5),
    .out6(demultiplexer_1_out6), .out7(demultiplexer_1_out7), .in(OPT0), .sel(in_8));
  Demultiplexer #(.select(3), .enable("false")) demultiplexer_2 (
    .out0(BEQ), .out1(BNE), .out2(BLEZ), .out3(BGTZ), .out4(BLTZ), .out5(J), .out6(JR), .in(OPT2), .sel(in_8));  // open: out7
  D_Flip_Flop #(.trigger("falling")) Halt (.clk(in_1), .D(TO_IDLE), .Q(LHALT0), .reset(in_3));  // open: Qn, preset, en
  not not_1 (A1____A2, in_2);
  or or_1 (or_1_out, demultiplexer_1_out0, demultiplexer_1_out1);
  or or_2 (out_34, demultiplexer_1_out2, demultiplexer_1_out3);
  or or_3 (or_3_out, demultiplexer_1_out4, demultiplexer_1_out5, demultiplexer_1_out6, demultiplexer_1_out7);
  D_Flip_Flop #(.trigger("falling")) IDLE (.clk(in_1), .D(or_4_out), .Q(IDLE_q), .preset(in_3));  // open: Qn, en, reset
  or or_4 (or_4_out, demultiplexer_3_out0, LHALT0);
  or or_5 (or_5_out, out_34, REGW0);
  or or_6 (REGW0, or_1_out, or_3_out);
  Demultiplexer #(.enable("false")) demultiplexer_3 (
    .out0(demultiplexer_3_out0), .out1(demultiplexer_3_out1), .in(IDLE_q), .sel(in_3));
  D_Flip_Flop #(.trigger("falling")) PC____4 (
    .clk(in_1), .D(WHILE_END), .Q(LPC0), .reset(in_3));  // open: Qn, preset, en
  or or_7 (WE0, or_5_out, REG00);
  Demultiplexer #(.enable("false")) demultiplexer_4 (.out0(demultiplexer_4_out0), .out1(BRANCH0), .in(BEQ), .sel(in_2));
  Demultiplexer #(.enable("false")) demultiplexer_5 (
    .out0(demultiplexer_5_out0), .out1(BRANCH1), .in(BNE), .sel(A1____A2));
  Demultiplexer #(.enable("false")) demultiplexer_6 (
    .out0(demultiplexer_6_out0), .out1(BRANCH2), .in(BGTZ), .sel(in_5));
  or or_8 (or_8_out, demultiplexer_3_out1, LPC0);
  Demultiplexer #(.enable("false")) demultiplexer_7 (.out0(L_A_0), .out1(TO_IDLE), .in(While_q), .sel(in_13));
  D_Flip_Flop #(.trigger("falling")) While (.clk(in_1), .D(or_8_out), .Q(While_q));  // open: Qn, preset, en, reset
  or or_9 (WE6, demultiplexer_6_out0, demultiplexer_5_out0, demultiplexer_4_out0, demultiplexer_9_out0, demultiplexer_10_out0);
  Demultiplexer #(.select(3), .enable("false")) demultiplexer_8 (
    .out0(REG00), .out1(L_TR_2), .out2(out_26), .out3(ADR10), .out4(LRAM1), .out5(MFHI), .out6(MFLO),
    .in(OPT1), .sel(in_8));  // open: out7
  or or_10 (BRANCH, BRANCH0, BRANCH3, BRANCH1, BRANCH2, BRANCH4);
  D_Flip_Flop #(.trigger("falling")) u_BRANCH (.clk(in_1), .D(BRANCH), .Q(WE4), .reset(in_3));  // open: Qn, preset, en
  Demultiplexer #(.enable("false")) demultiplexer_9 (
    .out0(demultiplexer_9_out0), .out1(BRANCH3), .in(BLEZ), .sel(in_7));
  Demultiplexer #(.enable("false")) demultiplexer_10 (
    .out0(demultiplexer_10_out0), .out1(BRANCH4), .in(BLTZ), .sel(in_9));
  D_Flip_Flop #(.trigger("falling")) Set_ADDR (
    .clk(in_1), .D(L_A_0), .Q(Set_ADDR_q), .reset(in_3));  // open: Qn, preset, en
  D_Flip_Flop #(.trigger("falling")) LOAD_RAM (
    .clk(in_1), .D(or_11_out), .Q(LOAD_RAM_q), .reset(in_3));  // open: Qn, preset, en
  or or_11 (or_11_out, demultiplexer_11_out0, Set_ADDR_q);
  Demultiplexer #(.enable("false")) demultiplexer_11 (
    .out0(demultiplexer_11_out0), .out1(demultiplexer_11_out1), .in(LOAD_RAM_q), .sel(in_4));
  or or_12 (or_12_out, demultiplexer_12_out0, L_TR_2);
  or or_13 (out_17[0], L_TR_2, out_26);
  or or_14 (LPC2, J, JR);
  or or_15 (CS0, LOAD_RAM_q, out_14);
  D_Flip_Flop #(.trigger("falling")) LOAD_RAM_2 (
    .clk(in_1), .D(or_12_out), .Q(LOAD_RAM_2_q), .reset(in_3));  // open: Qn, preset, en
  or or_16 (or_16_out, out_26, demultiplexer_13_out0);
  D_Flip_Flop #(.trigger("falling")) JUMP (.clk(in_1), .D(LPC2), .Q(WE5), .reset(in_3));  // open: Qn, preset, en
  D_Flip_Flop #(.trigger("falling")) CHANGE_TR (
    .clk(in_1), .D(demultiplexer_11_out1), .Q(out_14), .reset(in_3));  // open: Qn, preset, en
  or or_17 (CS4, LOAD_RAM_2_q, REG10);
  Demultiplexer #(.enable("false")) demultiplexer_12 (
    .out0(demultiplexer_12_out0), .out1(demultiplexer_12_out1), .in(LOAD_RAM_2_q), .sel(in_4));
  D_Flip_Flop #(.trigger("falling")) WRITE_RAM (
    .clk(in_1), .D(or_16_out), .Q(CS3), .reset(in_3));  // open: Qn, preset, en
  D_Flip_Flop #(.trigger("falling")) CHANGE_TR_2 (
    .clk(in_1), .D(out_14), .Q(out_15[0]), .reset(in_3));  // open: Qn, preset, en
  D_Flip_Flop #(.trigger("falling")) WRITE_REG (
    .clk(in_1), .D(demultiplexer_12_out1), .Q(REG10), .reset(in_3));  // open: Qn, preset, en
  Demultiplexer #(.enable("false")) demultiplexer_13 (
    .out0(demultiplexer_13_out0), .out1(demultiplexer_13_out1), .in(CS3), .sel(in_6));
  Demultiplexer #(.select(3), .enable("false")) demultiplexer_14 (
    .out0(demultiplexer_14_out0), .out1(out_20), .out2(out_18), .out3(L_TR_5), .out4(L_TR_6), .in(OPT3),
    .sel(in_8));  // open: out5, out6, out7
  D_Flip_Flop #(.trigger("falling")) SET_A1 (
    .clk(in_1), .D(out_15[0]), .Q(out_23), .reset(in_3));  // open: Qn, preset, en
  or or_18 (WE2, REG10, demultiplexer_13_out1);
  or or_19 (L_TR_0, out_15[0], CHANGE_TR_3_q, TR_1_0);
  D_Flip_Flop #(.trigger("falling")) CHANGE_TR_3 (
    .clk(in_1), .D(out_23), .Q(CHANGE_TR_3_q), .reset(in_3));  // open: Qn, preset, en
  Demultiplexer #(.enable("false")) demultiplexer_15 (.out0(REG02), .out1(out_22), .in(L_TR_6), .sel(in_11));
  D_Flip_Flop #(.trigger("falling")) SET_A2 (
    .clk(in_1), .D(CHANGE_TR_3_q), .Q(out_25), .reset(in_3));  // open: Qn, preset, en
  or or_20 (L_TR_4, MFHI, MFLO);
  D_Flip_Flop #(.trigger("falling")) CHANGE_TR_4 (
    .clk(in_1), .D(out_25), .Q(TR_1_0), .reset(in_3));  // open: Qn, preset, en
  D_Flip_Flop #(.trigger("falling")) SET_A3 (.clk(in_1), .D(TR_1_0), .Q(out_28), .reset(in_3));  // open: Qn, preset, en
  or or_21 (WE7, demultiplexer_14_out0, out_20, out_18, L_TR_5, L_TR_6);
  D_Flip_Flop #(.trigger("falling")) IF_I (.clk(in_1), .D(out_28), .Q(out_16), .reset(in_3));  // open: Qn, preset, en
  D_Flip_Flop #(.trigger("falling")) SP_W (.clk(in_1), .D(LRAM1), .Q(ADR11), .reset(in_3));  // open: Qn, preset, en
  Demultiplexer #(.enable("false")) demultiplexer_16 (
    .out0(TR_1_5), .out1(demultiplexer_16_out1), .in(out_16), .sel(in_12));
  or or_22 (or_22_out, demultiplexer_17_out0, ADR10);
  Demultiplexer #(.enable("false")) demultiplexer_17 (
    .out0(demultiplexer_17_out0), .out1(demultiplexer_17_out1), .in(LOAD_RAM_3_q), .sel(in_4));
  D_Flip_Flop #(.trigger("falling")) LOAD_RAM_3 (
    .clk(in_1), .D(or_22_out), .Q(LOAD_RAM_3_q), .reset(in_3));  // open: Qn, preset, en
  or or_23 (or_23_out, ADR11, demultiplexer_19_out0);
  D_Flip_Flop #(.trigger("falling")) LOAD (
    .clk(in_1), .D(or_24_out), .Q(LOAD_q), .reset(in_3));  // open: Qn, preset, en
  or or_24 (or_24_out, TR_1_5, demultiplexer_16_out1);
  D_Flip_Flop #(.trigger("falling")) WRITE_RAM_2 (
    .clk(in_1), .D(or_23_out), .Q(CS2), .reset(in_3));  // open: Qn, preset, en
  Demultiplexer #(.select(2), .enable("false")) demultiplexer_18 (
    .out0(OPT0), .out1(OPT1), .out2(OPT2), .out3(OPT3), .in(LOAD_q), .sel(in_10));
  or or_25 (CS1, LOAD_RAM_3_q, out_29);
  D_Flip_Flop #(.trigger("falling")) WRITE_REG_2 (
    .clk(in_1), .D(demultiplexer_17_out1), .Q(out_29), .reset(in_3));  // open: Qn, preset, en
  Demultiplexer #(.enable("false")) demultiplexer_19 (
    .out0(demultiplexer_19_out0), .out1(demultiplexer_19_out1), .in(CS2), .sel(in_6));
  or or_26 (WHILE_END, WE0, WE1, WE7, WE2, L_TR_4, WE4, WE5, WE6);
  or or_27 (out_36, out_26, LRAM1);
  or or_28 (out_37[0], REG00, MFHI, REG02);
  or or_29 (out_37[1], REG10, out_29, MFHI, L_TR_5, L_TR_6);
  or or_30 (out_37[2], MFLO, L_TR_5, L_TR_6);
  or or_31 (WE1, out_29, demultiplexer_19_out1);
  or or_32 (out_35, REGW0, REG00, REG10, L_TR_6, out_29, L_TR_4, L_TR_5);
  or or_33 (out_24[0], BRANCH, JR);
  or or_34 (out_30, LHALT0, out_20);
  or or_35 (out_32, LPC0, BRANCH, LPC2);
  or or_36 (out_15[1], TR_1_0, L_TR_4, ADR10, L_TR_5, L_TR_6, TR_1_5);
  or or_37 (out_19, L_TR_0, out_16, L_TR_2, ADR10, L_TR_4, L_TR_5, L_TR_6);
  or or_38 (out_31, CS0, CS1, CS2, CS3, CS4);
  or or_39 (out_33, out_29, LRAM1);
  or or_40 (out_17[1], ADR10, ADR11);
  or or_41 (out_27, CS2, CS3);
  or or_42 (out_24[1], J, JR);
  or or_43 (out_21, L_A_0, out_17[0], ADR11, ADR10);

  // Other names for the same wires on the sheet: A1___0 = in_9; A1___0_t = in_5; A1____0 = in_7; A1____A2_t = in_2;
  //   ADDR_0 = out_17[0]; ADDR_SEL[1:0] = out_17; L_A_1 = out_17[0]; ADDR_1 = out_17[1]; CLK = in_1; CLR = in_3;
  //   CS = out_31; HALT = in_13; I = in_12; KBD_AVAIL = in_11; KBD_ENABLE = out_22; L_A1 = out_23; L_A2 = out_25;
  //   L_A3 = out_28; L_A_3 = ADR11; L_ADDR = out_21; L_HALT = out_30; L_HiLo = out_34; L_INS = out_14; L_PC = out_32;
  //   L_RAM_IN = out_36; L_TARGET_REG = out_19; L_ALU_IN_B = out_16; L_TR_1 = out_16; HALT_IN = out_20;
  //   LHALT1 = out_20; LW = L_TR_2; OP[2:0] = in_8; OPT[1:0] = in_10; PC_IN_SEL[1:0] = out_24; PCI0 = out_24[0];
  //   PCI1 = out_24[1]; LPC1 = BRANCH; PCI00 = BRANCH; PCI10 = J; PCI01 = JR; PCI11 = JR; RAM_READ = in_4;
  //   RAM_WRITE = in_6; REG01 = MFHI; REG12 = MFHI; REG20 = MFLO; REG0 = out_37[0]; REG_IN_SEL[2:0] = out_37;
  //   REG1 = out_37[1]; REG2 = out_37[2]; REG_W = out_35; REGW2 = REG10; RW = out_27; RW0 = CS2; RW1 = CS3;
  //   REGW1 = REG00; SLT = REG00; SP_W = out_33; REG11 = out_29; REGW3 = out_29; SP_plus_plus = out_29; SPW0 = out_29;
  //   PUSH = LRAM1; SPW1 = LRAM1; LRAM0 = out_26; RAM_IN_SEL = out_26; SW = out_26; TARGET_REG_SEL[1:0] = out_15;
  //   TR_0 = out_15[0]; TR_1 = out_15[1]; L_A_2 = ADR10; L_TR_3 = ADR10; POP = ADR10; TR_1_1 = ADR10; REG13 = L_TR_5;
  //   REG21 = L_TR_5; REGW5 = L_TR_5; TR_1_3 = L_TR_5; REG14 = L_TR_6; REG22 = L_TR_6; REGW6 = L_TR_6;
  //   TR_1_4 = L_TR_6; TTY_ENABLE = out_18; REGW4 = L_TR_4; TR_1_2 = L_TR_4; WE3 = L_TR_4
endmodule

module DATA_PATH (
  input  in_1,
  input  [31:0] CURRENT_BANK,
  input  in_3,
  input  in_4,
  input  CLR,
  input  in_6,
  input  CLK,
  input  in_8,
  input  in_9,
  input  in_10,
  input  [1:0] in_11,
  input  in_12,
  input  in_13,
  input  [1:0] in_14,
  input  in_15,
  input  in_16,
  input  [6:0] in_17,
  input  in_18,
  input  in_19,
  input  in_20,
  input  [1:0] in_21,
  input  in_22,
  input  in_23,
  input  [2:0] in_24,
  output out_25,
  output out_26,
  output out_27,
  output out_28,
  output [6:0] out_29,
  output out_30,
  output [2:0] out_31,
  output [31:0] out_32,
  output [1:0] out_33,
  output out_34,
  output [31:0] out_35
);

  wire and_1_out, and_2_out, and_3_out, and_4_out, and_5_out, and_6_out, and_7_out, and_8_out, and_9_out,
       and_10_out, and_11_out, comparator_2_eq, EQ, GR, LS, not_1_out, not_2_out, not_3_out, U;
  wire [4:0] ARG_1, ARG_2, ARG_3, multiplexer_3_out, TARGET_REG;
  wire [13:0] bit_extender_1_out;
  wire [15:0] CONST;
  wire [25:0] JUMP_D;
  wire [31:0] A2, A3, adder_1_out, adder_2_out, adder_3_out, adder_4_out, ALU_IN_B, ALU_OUT, ALU_OUT_2,
       bit_extender_2_out, bit_extender_3_out, bit_extender_4_out, bit_extender_5_out, Hi, INS, Lo,
       multiplexer_1_out, multiplexer_2_out, multiplexer_4_out, multiplexer_5_out, multiplexer_6_out, PC,
       random_1_out, REG_IN, REG_OUT, SP, SP_IN, subtractor_1_out, subtractor_2_out, subtractor_3_out;
  wire [31:7] A1;

  Register #(.width(32)) u_INS (.D(CURRENT_BANK), .Q(INS), .clk(and_1_out), .clr(CLR));  // open: en
  and and_1 (and_1_out, in_1, CLK);
  assign bit_extender_1_out = {{13{CONST[15]}}, CONST[15]};  // Bit_Extender bit_extender_1
  assign bit_extender_2_out = {{16{CONST[15]}}, CONST};  // Bit_Extender bit_extender_2
  Multiplexer #(.width(32), .enable("false")) multiplexer_1 (
    .in0(A2), .in1(bit_extender_2_out), .out(multiplexer_1_out), .sel(out_34));
  Adder #(.width(32)) adder_1 (.a({bit_extender_1_out, CONST, 2'b00}), .b(PC), .out(adder_1_out));  // open: cin, cout
  Adder #(.width(32)) adder_2 (.a(PC), .b(32'h4), .out(adder_2_out));  // open: cin, cout
  Register #(.width(1)) HALT (.D(in_18), .Q(out_30), .clk(and_2_out), .clr(CLR));  // open: en
  and and_2 (and_2_out, in_15, CLK);
  Register #(.width(32)) u_ALU_IN_B (.D(multiplexer_1_out), .Q(ALU_IN_B), .clk(and_3_out), .clr(CLR));  // open: en
  and and_3 (and_3_out, in_3, CLK);
  Multiplexer #(.select(2), .width(32), .enable("false")) multiplexer_2 (
    .in0(adder_2_out), .in1(adder_1_out), .in2(subtractor_1_out), .in3(subtractor_2_out),
    .out(multiplexer_2_out), .sel(in_21));
  and and_4 (and_4_out, in_16, CLK);
  Register #(.width(32)) u_PC (.D(multiplexer_2_out), .Q(PC), .clk(and_4_out), .clr(CLR));  // open: en
  Multiplexer #(.select(2), .width(5), .enable("false")) multiplexer_3 (
    .in0(ARG_2), .in1(ARG_1), .in2(ARG_3), .out(multiplexer_3_out), .sel(in_11));  // open: in3
  Register #(.width(5)) u_TARGET_REG (.D(multiplexer_3_out), .Q(TARGET_REG), .clk(and_5_out), .clr(CLR));  // open: en
  and and_5 (and_5_out, in_4, CLK);
  Subtractor #(.width(32)) subtractor_1 (
    .a({PC[31:28], JUMP_D, 2'b00}), .b(32'h4), .out(subtractor_1_out));  // open: bin, bout
  Subtractor #(.width(32)) subtractor_2 (.a({A1, out_29}), .b(32'h4), .out(subtractor_2_out));  // open: bin, bout
  assign bit_extender_3_out = {{16{CONST[15]}}, CONST};  // Bit_Extender bit_extender_3
  Register #(.width(32)) u_Hi (.D(ALU_OUT_2), .Q(Hi), .clk(and_6_out), .clr(CLR));  // open: en
  and and_6 (and_6_out, in_19, CLK);
  Adder #(.width(32)) adder_3 (.a({A1, out_29}), .b(bit_extender_3_out), .out(adder_3_out));  // open: cin, cout
  Multiplexer #(.select(2), .width(32), .enable("false")) multiplexer_4 (
    .in0(PC), .in1(adder_3_out), .in2(SP), .out(multiplexer_4_out), .sel(in_14));  // open: in3
  and and_7 (and_7_out, in_6, CLK);
  Register #(.width(32)) ADDR (.D(multiplexer_4_out), .Q(out_32), .clk(and_7_out), .clr(CLR));  // open: en
  Multiplexer #(.width(32), .enable("false")) multiplexer_5 (
    .in0({A1, out_29}), .in1(A2), .out(multiplexer_5_out), .sel(in_23));
  Register #(.width(32)) u_Lo (.D(ALU_OUT), .Q(Lo), .clk(and_6_out), .clr(CLR));  // open: en
  Register #(.width(32)) u_A1 (.D(REG_OUT), .Q({A1, out_29}), .clk(and_8_out), .clr(CLR));  // open: en
  and and_8 (and_8_out, in_8, CLK);
  Register #(.width(32)) RAM_IN (.D(multiplexer_5_out), .Q(out_35), .clk(and_9_out), .clr(CLR));  // open: en
  and and_9 (and_9_out, in_22, CLK);
  Comparator #(.width(32)) comparator_1 (.a({A1, out_29}), .b(A2), .eq(out_25));  // open: gt, lt
  Comparator #(.width(32)) comparator_2 (
    .a({A1, out_29}), .b({32{1'b0}}), .gt(out_26), .eq(comparator_2_eq), .lt(out_28));
  and and_10 (and_10_out, in_9, CLK);
  or or_1 (out_27, out_28, comparator_2_eq);
  Register #(.width(32)) u_A2 (.D(REG_OUT), .Q(A2), .clk(and_10_out), .clr(CLR));  // open: en
  Adder #(.width(32)) adder_4 (.a(SP), .b(32'h4), .out(adder_4_out));  // open: cin, cout
  Subtractor #(.width(32)) subtractor_3 (.a(SP), .b(32'h4), .out(subtractor_3_out));  // open: bin, bout
  Register #(.width(32)) u_A3 (.D(REG_OUT), .Q(A3), .clk(and_11_out), .clr(CLR));  // open: en
  and and_11 (and_11_out, in_12, CLK);
  Multiplexer #(.width(32), .enable("false")) multiplexer_6 (
    .in0(subtractor_3_out), .in1(adder_4_out), .out(multiplexer_6_out), .sel(in_10));
  Multiplexer #(.width(32), .enable("false")) multiplexer_7 (
    .in0(SP), .in1(multiplexer_6_out), .out(SP_IN), .sel(in_13));
  ID id_1 (
    .INSTRUCTION(INS), .OP(out_31), .OP_TYPE(out_33), .I(out_34), .U(U), .out_7(ARG_1), .out_8(ARG_2),
    .out_9(ARG_3), .out_10(JUMP_D), .out_11(CONST), .EN(not_1_out));
  not not_1 (not_1_out, CLR);
  not not_2 (not_2_out, GR);
  not not_3 (not_3_out, CLR);
  assign bit_extender_4_out = {{25{1'b0}}, in_17};  // Bit_Extender bit_extender_4
  Random #(.width(32), .seed(2)) random_1 (.clk(CLK), .out(random_1_out));  // open: next, clr
  assign bit_extender_5_out = {{31{1'b0}}, not_2_out};  // Bit_Extender bit_extender_5
  Multiplexer #(.select(3), .width(32), .enable("false")) multiplexer_8 (
    .in0(ALU_OUT), .in1(bit_extender_5_out), .in2(CURRENT_BANK), .in3(Hi), .in4(Lo), .in5(random_1_out),
    .in6(bit_extender_4_out), .in7({32{1'b1}}), .out(REG_IN), .sel(in_24));
  RF rf_1 (
    .WRITE(in_20), .IN(REG_IN), .SEL(TARGET_REG), .OUT(REG_OUT), .CLK(CLK), .RST(CLR), .SP_IN(SP_IN),
    .SP_OUT(SP));
  ALU alu_1 (
    .IN_A({A1, out_29}), .IN_B(ALU_IN_B), .U(U), .SEL(out_31), .OUT1(ALU_OUT), .OUT2(ALU_OUT_2), .out_8(EQ),
    .out_9(LS), .out_7(GR));

  // Other names for the same wires on the sheet: A1___0 = out_28; A1___0_t = out_26; A1____0 = out_27;
  //   A1____A2 = out_25; ADDR[31:0] = out_32; ADDR_SEL[1:0] = in_14; A1[6:0] = out_29; ALU_IN_A[31:0] = {A1, out_29};
  //   HALT = out_30; HALT_IN = in_18; I = out_34; KBD_DATA[6:0] = in_17; L_A1 = in_8; L_A2 = in_9; L_A3 = in_12;
  //   L_ADDR = in_6; L_ALU_IN_B = in_3; L_HALT = in_15; L_HiLo = in_19; L_INS = in_1; L_PC = in_16; L_RAM_IN = in_22;
  //   L_TARGET_REG = in_4; OP[2:0] = out_31; OPT[1:0] = out_33; PC_IN_SEL[1:0] = in_21; RAM_IN[31:0] = out_35;
  //   RAM_IN_SEL = in_23; REG_IN_SEL[2:0] = in_24; REG_W = in_20; SP_plus_plus = in_10; SP_W = in_13;
  //   TARGET_REG_SEL[1:0] = in_11

  // Notes on the sheet:
  //   INSTRUCTION DECODER
  //   REGISTRY FETCH
  //   ALU
endmodule
